# Fritzing sketch edison-bot (saved by Fritzing 0.9.1b)
stripboards: 1

parts:
  Part1 = DRV8835 Breakout
  M5 = DC Motor  # not connected
  M6 = DC Motor  # not connected
  BAT2 = BC9VPC [package=bc9vpc]
  BAT1 = BC9VPC [package=bc9vpc]  # not connected
  U1 = EDISON

nets:
  N1: Part1.GND, BAT2.V-
  VIN: Part1.VIN, Part1.VCC, BAT2.V+
  N2: Part1.DIRB, U1.GP27
  N3: Part1.PWMA, U1.GP182_PWM2
  N4: Part1.DIRA, U1.GP135
  N5: Part1.MODE, U1.GND
  N6: Part1.PWMB, U1.GP13_PWM1

custom parts:
  DC Motor: Your standard DC Motor
