# Fritzing sketch imp-bot (saved by Fritzing 0.9.1b)
stripboards: 1

parts:
  Part1 = DRV8835 Breakout
  M5 = DC Motor  # not connected
  M6 = DC Motor  # not connected
  BAT2 = BC9VPC [package=bc9vpc]
  Part2 = Electric Imp April
  BAT1 = BC9VPC [package=bc9vpc]

nets:
  N1: Part1.GND, BAT2.V-
  VIN: Part1.VIN, Part1.VCC, BAT2.V+
  N2: Part1.DIRB, Part2.6
  N3: Part1.PWMA, Part2.3
  N4: Part1.DIRA, Part2.4
  N5: Part1.MODE, Part2.9
  N6: Part1.PWMB, Part2.5
  N7: Part2.10, BAT1.V+
  N8: Part2.11, BAT1.V-

custom parts:
  DC Motor: Your standard DC Motor
  Electric Imp April: Electric Imp Breakout Board with onboard 3.3V regulated power supply
