# Fritzing sketch particle-bot (saved by Fritzing 0.9.1b)
stripboards: 1

parts:
  Part1 = DRV8835 Breakout
  U1 = Spark Core (v1.0)
  BAT1 = BC9VPC [package=bc9vpc]
  M5 = DC Motor  # not connected
  M6 = DC Motor  # not connected
  BAT2 = BC9VPC [package=bc9vpc]

nets:
  N1: Part1.GND, BAT2.V-
  VIN: Part1.VIN, Part1.VCC, BAT2.V+
  N2: Part1.DIRB, U1.D3
  N3: Part1.PWMA, U1.D0
  N4: Part1.DIRA, U1.D2
  N5: Part1.MODE, U1.A2, U1.3V3
  N6: Part1.PWMB, U1.D1
  N7: U1.A5, U1.VIN, BAT1.V+
  N8: U1.GND, BAT1.V-

custom parts:
  Spark Core (v1.0): The Spark Core is a tiny Wi-Fi development board that makes it easy to create internet-connected hardware. The Core is all you need to get started; power it over USB and in minutes you'll be controlling LEDs, switches and motors and collecting data from sensors over the internet! It has 8 digital I/O pins, 8 analog I/O pins, 8 PWM pins; UART (Serial), SPI, I2C, and JTAG peripherals available.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
  DC Motor: Your standard DC Motor
